// Logisim project Mano Machine.circ as structural Verilog: 27 circuits, main circuit main
module main (
  input  [7:0] INP,
  output [2:0] out_2
);

  wire ac_control_1_clr, ac_control_1_inc, alu_1_e_out, and_1_out, ar_control_1_clr, ar_control_1_inc,
       ar_control_1_ld, clear_t_count_control_1_t_count_clear, clock_1_out, Clr_T_count, dr_control_1_inc,
       dr_control_1_ld, E, e_control_1_clear, e_control_1_comp, e_control_1_load, FGI,
       fgi_o_ien_control_1_fgi_j, fgi_o_ien_control_1_fgi_k, fgi_o_ien_control_1_fgo_j,
       fgi_o_ien_control_1_fgo_k, fgi_o_ien_control_1_ien_j, fgi_o_ien_control_1_ien_k, FGO, HLT, I,
       ien_1_ein_out, ir_control_1_ld, j_k_ff_1_q, memory_control_1_load, not_1_out, outpr_control_1_ld,
       pc_control_1_clr, pc_control_1_inc, pc_control_1_ld, R, tr_control_1_ld;
  wire [2:0] T_count;
  wire [3:0] _3_0_OUT, _7_4_OUT, alu_1_out, alu_1_out_2, alu_1_out_3, alu_1_out_4, ar_1_bus_out,
       ar_1_bus_out_2, ar_1_bus_out_3, ar_1_bus_out_4, multiplexer_1_out, multiplexer_1_out_2, outr_1_hex_0,
       outr_1_hex_1, pc_1_bus_out, pc_1_bus_out_2, pc_1_bus_out_3, pc_1_bus_out_4;
  wire [15:0] AC, controlled_buffer_1_out, controlled_buffer_2_out, DR, IR, tr_1_bus_out;

  Bus_Select_control bus_select_control_1 (.T({1'b0, T_count}), .R(R), .IR(IR), .Bus_Select(out_2));
  Clear_T_count_control clear_t_count_control_1 (
    .T_count_clear(clear_t_count_control_1_t_count_clear), .T({1'b0, T_count}), .R(R), .IR(IR));
  or or_1 (Clr_T_count, HLT, clear_t_count_control_1_t_count_clear);
  OUTPR_control outpr_control_1 (.LD(outpr_control_1_ld), .T({1'b0, T_count}), .IR(IR));
  TR_control tr_control_1 (.LD(tr_control_1_ld), .T({1'b0, T_count}), .R(R));
  IR_control ir_control_1 (.LD(ir_control_1_ld), .T({1'b0, T_count}), .R(R));
  DR_control dr_control_1 (.LD(dr_control_1_ld), .Inc(dr_control_1_inc), .T({1'b0, T_count}), .IR(IR));
  PC_control pc_control_1 (
    .LD(pc_control_1_ld), .Inc(pc_control_1_inc), .Clr(pc_control_1_clr), .T({1'b0, T_count}), .FGI(FGI),
    .FGO(FGO), .E(E), .R(R), .IR(IR), .DR(DR), .AC(AC));
  AR_control ar_control_1 (
    .LD(ar_control_1_ld), .Clr(ar_control_1_clr), .Inc(ar_control_1_inc), .T({1'b0, T_count}), .R(R), .IR(IR));
  AC_control ac_control_1 (.Clr(ac_control_1_clr), .Inc(ac_control_1_inc), .T({1'b0, T_count}), .IR(IR));
  OUTR outr_1 (
    .BUS_IN({multiplexer_1_out_2, multiplexer_1_out, _7_4_OUT, _3_0_OUT}), .L_OUT(outpr_control_1_ld),
    .Clock(and_1_out), .Hex_0(outr_1_hex_0), .Hex_1(outr_1_hex_1));
  Hex_Digit_Display hex_digit_display_1 (.value(DR[15:12]));  // open: dp
  DR dr_1 (
    .Bus_OUT(DR), .Load(dr_control_1_ld), .Clock(and_1_out), .Inc(dr_control_1_inc),
    .Bus_IN({multiplexer_1_out_2, multiplexer_1_out, _7_4_OUT, _3_0_OUT}));  // open: Clear
  Hex_Digit_Display hex_digit_display_2 (.value(tr_1_bus_out[15:12]));  // open: dp
  TR tr_1 (
    .Bus_OUT(tr_1_bus_out), .Clock(and_1_out), .Load(tr_control_1_ld),
    .Bus_IN({multiplexer_1_out_2, multiplexer_1_out, _7_4_OUT, _3_0_OUT}));  // open: Inc, Clear
  Hex_Digit_Display hex_digit_display_3 (.value(IR[15:12]));  // open: dp
  IR ir_1 (
    .Bus_OUT(IR), .Clock(and_1_out), .Load(ir_control_1_ld),
    .Bus_IN({multiplexer_1_out_2, multiplexer_1_out, _7_4_OUT, _3_0_OUT}), .I(I), .S(HLT));
  Hex_Digit_Display hex_digit_display_4 (.value(pc_1_bus_out_4));  // open: dp
  PC pc_1 (
    .Bus_OUT({pc_1_bus_out_4, pc_1_bus_out_3, pc_1_bus_out_2, pc_1_bus_out}), .Clear(pc_control_1_clr),
    .Clock(and_1_out), .Load(pc_control_1_ld), .Inc(pc_control_1_inc),
    .Bus_IN({multiplexer_1_out_2, multiplexer_1_out, _7_4_OUT, _3_0_OUT}));
  AR ar_1 (
    .Bus_OUT({ar_1_bus_out, ar_1_bus_out_4, ar_1_bus_out_3, ar_1_bus_out_2}), .Clear(ar_control_1_clr),
    .Clock(and_1_out), .Load(ar_control_1_ld), .Inc(ar_control_1_inc),
    .Bus_IN({multiplexer_1_out_2, multiplexer_1_out, _7_4_OUT, _3_0_OUT}));
  AC ac_1 (
    .Bus_OUT(AC), .Clear(ac_control_1_clr), .Clock(and_1_out), .Inc(ac_control_1_inc),
    .ALU_In({alu_1_out_4, alu_1_out_3, alu_1_out_2, alu_1_out}));
  Hex_Digit_Display hex_digit_display_5 (.value(DR[7:4]));  // open: dp
  Hex_Digit_Display hex_digit_display_6 (.value(DR[11:8]));  // open: dp
  Hex_Digit_Display hex_digit_display_7 (.value(tr_1_bus_out[7:4]));  // open: dp
  Hex_Digit_Display hex_digit_display_8 (.value(tr_1_bus_out[11:8]));  // open: dp
  Hex_Digit_Display hex_digit_display_9 (.value(IR[7:4]));  // open: dp
  Hex_Digit_Display hex_digit_display_10 (.value(IR[11:8]));  // open: dp
  Hex_Digit_Display hex_digit_display_11 (.value(pc_1_bus_out_2));  // open: dp
  Hex_Digit_Display hex_digit_display_12 (.value(pc_1_bus_out_3));  // open: dp
  Hex_Digit_Display hex_digit_display_13 (.value(ar_1_bus_out_4));  // open: dp
  Hex_Digit_Display hex_digit_display_14 (.value(ar_1_bus_out));  // open: dp
  Hex_Digit_Display hex_digit_display_15 (.value(AC[15:12]));  // open: dp
  Hex_Digit_Display hex_digit_display_16 (.value(AC[11:8]));  // open: dp
  Hex_Digit_Display hex_digit_display_17 (.value(DR[3:0]));  // open: dp
  Hex_Digit_Display hex_digit_display_18 (.value(tr_1_bus_out[3:0]));  // open: dp
  Hex_Digit_Display hex_digit_display_19 (.value(IR[3:0]));  // open: dp
  Hex_Digit_Display hex_digit_display_20 (.value(pc_1_bus_out));  // open: dp
  Hex_Digit_Display hex_digit_display_21 (.value(ar_1_bus_out_3));  // open: dp
  Hex_Digit_Display hex_digit_display_22 (.value(ar_1_bus_out_2));  // open: dp
  Hex_Digit_Display hex_digit_display_23 (.value(AC[7:4]));  // open: dp
  Hex_Digit_Display hex_digit_display_24 (.value(AC[3:0]));  // open: dp
  Hex_Digit_Display hex_digit_display_25 (.value(outr_1_hex_0));  // open: dp
  Hex_Digit_Display hex_digit_display_26 (.value(outr_1_hex_1));  // open: dp
  Memory_control memory_control_1 (.Load(memory_control_1_load), .T({1'b0, T_count}), .R(R), .IR(IR));
  assign controlled_buffer_1_out = not_1_out ? {multiplexer_1_out_2, multiplexer_1_out, _7_4_OUT, _3_0_OUT} : 16'bz;  // Controlled_Buffer controlled_buffer_1
  assign controlled_buffer_2_out = memory_control_1_load ? controlled_buffer_1_out : 16'bz;  // Controlled_Buffer controlled_buffer_2
  RAM #(.addrWidth(12), .dataWidth(16)) ram_1 (
    .addr({ar_1_bus_out_4, ar_1_bus_out_3, ar_1_bus_out_2}), .data(controlled_buffer_1_out), .clk(and_1_out),
    .ld(memory_control_1_load));  // open: sel, clr
  not not_1 (not_1_out, memory_control_1_load);
  Hex_Digit_Display hex_digit_display_27 (.value(alu_1_out_4));  // open: dp
  Hex_Digit_Display hex_digit_display_28 (.value(multiplexer_1_out_2));  // open: dp
  Hex_Digit_Display hex_digit_display_29 (.value(alu_1_out_2));  // open: dp
  Hex_Digit_Display hex_digit_display_30 (.value(alu_1_out_3));  // open: dp
  Hex_Digit_Display hex_digit_display_31 (.value(_7_4_OUT));  // open: dp
  Hex_Digit_Display hex_digit_display_32 (.value(multiplexer_1_out));  // open: dp
  ALU alu_1 (
    .OUT({alu_1_out_4, alu_1_out_3, alu_1_out_2, alu_1_out}), .DR(DR), .INPR(INP), .AC(AC),
    .E_Out(alu_1_e_out), .E_In(E), .IR(IR), .T({1'b0, T_count}));
  Hex_Digit_Display hex_digit_display_33 (.value(alu_1_out));  // open: dp
  Hex_Digit_Display hex_digit_display_34 (.value(_3_0_OUT));  // open: dp
  E e_1 (
    .E_OUT(E), .E_IN(alu_1_e_out), .Comp(e_control_1_comp), .Clock(and_1_out), .Clear(e_control_1_clear),
    .load(e_control_1_load));
  Multiplexer #(.select(3), .width(16)) multiplexer_1 (
    .in1({ar_1_bus_out, ar_1_bus_out_4, ar_1_bus_out_3, ar_1_bus_out_2}),
    .in2({pc_1_bus_out_4, pc_1_bus_out_3, pc_1_bus_out_2, pc_1_bus_out}), .in3(DR), .in4(AC), .in5(IR),
    .in6(tr_1_bus_out), .in7(controlled_buffer_2_out),
    .out({multiplexer_1_out_2, multiplexer_1_out, _7_4_OUT, _3_0_OUT}), .sel(out_2));  // open: in0, en
  LED E_2 (.in(E));
  E_control e_control_1 (
    .Comp(e_control_1_comp), .Clear(e_control_1_clear), .IR(IR), .T({1'b0, T_count}), .Load(e_control_1_load));
  // Probe on multiplexer_1_out_2[3]
  LED u_I (.in(I));
  LED I_EN (.in(ien_1_ein_out));
  IEN ien_1 (
    .EIN_J(fgi_o_ien_control_1_ien_j), .EIN_OUT(ien_1_ein_out), .EIN_K(fgi_o_ien_control_1_ien_k),
    .Clock(and_1_out));
  FGI fgi_1 (.FGI_J(fgi_o_ien_control_1_fgi_j), .FGI_OUT(FGI), .FGI_K(fgi_o_ien_control_1_fgi_k), .Clock(and_1_out));
  FGI_O___IEN_control fgi_o_ien_control_1 (
    .IEN_J(fgi_o_ien_control_1_ien_j), .IEN_K(fgi_o_ien_control_1_ien_k), .FGI_J(fgi_o_ien_control_1_fgi_j),
    .FGI_K(fgi_o_ien_control_1_fgi_k), .FGO_J(fgi_o_ien_control_1_fgo_j), .FGO_K(fgi_o_ien_control_1_fgo_k),
    .T({1'b0, T_count}), .INPR(INP), .R(R), .IR(IR));
  // Probe on multiplexer_1_out_2[2]
  // Probe on multiplexer_1_out_2[1]
  // Probe on multiplexer_1_out_2[0]
  LED u_R (.in(R));
  R r_2 (.E_IN(ien_1_ein_out), .E_OUT(R), .T_count(T_count), .FGO(FGO), .FGI(FGI));
  FGO fgo_1 (.FGO_J(fgi_o_ien_control_1_fgo_j), .FGO_OUT(FGO), .FGO_K(fgi_o_ien_control_1_fgo_k), .Clock(and_1_out));
  // Probe on multiplexer_1_out[2]
  // Probe on multiplexer_1_out[3]
  LED FGI_2 (.in(FGI));
  // Probe on multiplexer_1_out[0]
  // Probe on _7_4_OUT[3]
  // Probe on _7_4_OUT[2]
  // Probe on multiplexer_1_out[1]
  LED FGO_2 (.in(FGO));
  // Probe on _7_4_OUT[1]
  // Probe on _3_0_OUT[3]
  // Probe on _7_4_OUT[0]
  Hex_Digit_Display hex_digit_display_35 (.value({1'b0, T_count}));  // open: dp
  // Probe on _3_0_OUT[1]
  // Probe on _3_0_OUT[2]
  // Probe on _3_0_OUT[0]
  Hex_Digit_Display hex_digit_display_36 (.value({1'b0, T_count}));  // open: dp
  T_count t_count_1 (.OUT(T_count), .Clear(Clr_T_count), .Clock(and_1_out));
  Clock clock_1 (.out(clock_1_out));
  and and_1 (and_1_out, clock_1_out, j_k_ff_1_q);
  J_K_Flip_Flop j_k_ff_1 (.J(1'b0), .clk(clock_1_out), .K(HLT), .Q(j_k_ff_1_q));  // open: Qn, preset, en, reset

  // Other names for the same wires on the sheet: S[2:0] = out_2

  // Notes on the sheet:
  //   OUT
  //   BUS value in HEX
  //   BUS 15 14 13 12 11 10  9  8  7  6  5  4  3   2  1  0
  //   SC
  //   T count
  //   Clock
  //   **Enable clock at the beginning by clicking
  //    on that JK Flip flop to set it to 1**
endmodule

module ALU (
  input  [3:0] T,
  input  [15:0] IR,
  input  [7:0] INPR,
  input  [15:0] DR,
  input  E_In,
  input  [15:0] AC,
  output [15:0] OUT,
  output E_Out
);

  wire adder_1_cout, and_2_out, and_3_out, and_4_out, and_7_out, and_8_out, and_9_out, and_10_out,
       and_11_out, and_12_out, and_13_out, decoder_1_out0, decoder_1_out1, decoder_1_out2, decoder_1_out3,
       decoder_1_out4, decoder_1_out5, decoder_1_out6, decoder_1_out7, decoder_2_out0, decoder_2_out1,
       decoder_2_out2, decoder_2_out3, decoder_2_out4, decoder_2_out5, decoder_2_out6, decoder_2_out7,
       not_2_out, or_1_out, p, r;
  wire [2:0] S;
  wire [15:0] adder_1_out, and_1_out, not_1_out, register_1_q, register_2_q, shifter_1_out, shifter_2_out;

  Shifter #(.width(16)) shifter_1 (.in(AC), .\dist (4'b0001), .out(shifter_1_out));
  Shifter #(.width(16), .shift("lr")) shifter_2 (.in(AC), .\dist (4'b0001), .out(shifter_2_out));
  assign not_1_out = ~AC;  // NOT_Gate not_1, 16 bits wide
  assign and_1_out = AC & DR;  // AND_Gate and_1, 16 bits wide
  Adder #(.width(16)) adder_1 (.a(DR), .b(AC), .out(adder_1_out), .cout(adder_1_cout));  // open: cin
  Register #(.width(16), .trigger("high")) register_1 (
    .D({E_In, shifter_2_out[14:0]}), .Q(register_1_q), .clk(1'b1));  // open: en, clr
  and and_2 (and_2_out, S[2], S[1], ~S[0]);  // AND_Gate
  and and_3 (and_3_out, S[2], ~S[1], ~S[0]);  // AND_Gate
  assign E_Out = and_3_out ? AC[0] : 1'bz;  // Controlled_Buffer controlled_buffer_1
  assign E_Out = and_2_out ? adder_1_cout : 1'bz;  // Controlled_Buffer controlled_buffer_2
  Register #(.width(16), .trigger("high")) register_2 (
    .D({shifter_1_out[15:1], E_In}), .Q(register_2_q), .clk(1'b1));  // open: en, clr
  and and_4 (and_4_out, ~S[2], S[1], S[0]);  // AND_Gate
  assign E_Out = and_4_out ? AC[15] : 1'bz;  // Controlled_Buffer controlled_buffer_3
  Multiplexer #(.select(3), .width(16)) multiplexer_1 (
    .in0(AC), .in1(DR), .in2(not_1_out), .in3(register_2_q), .in4(register_1_q), .in5(and_1_out),
    .in6(adder_1_out), .in7({{8{1'b0}}, INPR}), .out(OUT), .sel(S));  // open: en
  Decoder #(.select(3)) decoder_1 (
    .out0(decoder_1_out0), .out1(decoder_1_out1), .out2(decoder_1_out2), .out3(decoder_1_out3),
    .out4(decoder_1_out4), .out5(decoder_1_out5), .out6(decoder_1_out6), .out7(decoder_1_out7), .sel(T[2:0]));  // open: en
  Decoder #(.select(3)) decoder_2 (
    .out0(decoder_2_out0), .out1(decoder_2_out1), .out2(decoder_2_out2), .out3(decoder_2_out3),
    .out4(decoder_2_out4), .out5(decoder_2_out5), .out6(decoder_2_out6), .out7(decoder_2_out7),
    .sel(IR[14:12]));  // open: en
  and and_5 (r, decoder_2_out7, ~IR[15], decoder_1_out3);  // AND_Gate
  and and_6 (p, decoder_2_out7, IR[15], decoder_1_out3);
  and and_7 (and_7_out, decoder_2_out0, decoder_1_out5);
  and and_8 (and_8_out, decoder_2_out1, decoder_1_out5);
  and and_9 (and_9_out, decoder_2_out2, decoder_1_out5);
  and and_10 (and_10_out, IR[9], r);
  and and_11 (and_11_out, IR[7], r);
  and and_12 (and_12_out, IR[6], r);
  and and_13 (and_13_out, IR[11], p);
  or or_1 (or_1_out, and_9_out, and_10_out, and_12_out, and_11_out, and_7_out, and_8_out, and_13_out);
  not not_2 (not_2_out, or_1_out);
  Priority_Encoder priority_encoder_1 (
    .in0(not_2_out), .in1(and_9_out), .in2(and_10_out), .in3(and_12_out), .in4(and_11_out), .in5(and_7_out),
    .in6(and_8_out), .in7(and_13_out), .out(S));  // open: en_in, gs, en_out
endmodule

module AC (
  input  Clear,
  input  Clock,
  input  Inc,
  input  [15:0] ALU_In,
  output [15:0] Bus_OUT
);

  wire [15:0] adder_1_out, multiplexer_1_out;

  Multiplexer #(.width(16)) multiplexer_1 (
    .in0(ALU_In), .in1(adder_1_out), .out(multiplexer_1_out), .sel(Inc));  // open: en
  Register #(.width(16), .trigger("falling")) register_1 (
    .D(multiplexer_1_out), .Q(Bus_OUT), .clk(Clock), .clr(Clear));  // open: en
  Adder #(.width(16)) adder_1 (.a(16'h1), .b(Bus_OUT), .out(adder_1_out));  // open: cin, cout
endmodule

module PC (
  input  [15:0] Bus_IN,
  input  Clear,
  input  Clock,
  input  Load,
  input  Inc,
  output [15:0] Bus_OUT
);

  wire or_1_out;
  wire [11:0] adder_1_out, multiplexer_1_out;

  Multiplexer #(.width(12)) multiplexer_1 (
    .in0(Bus_IN[11:0]), .in1(adder_1_out), .out(multiplexer_1_out), .sel(Inc));  // open: en
  or or_1 (or_1_out, Inc, Load);
  Register #(.width(12)) register_1 (.D(multiplexer_1_out), .en(or_1_out), .Q(Bus_OUT[11:0]), .clk(Clock), .clr(Clear));
  Adder #(.width(12)) adder_1 (.a(12'h1), .b(Bus_OUT[11:0]), .out(adder_1_out));  // open: cin, cout

  assign Bus_OUT[15:12] = 4'b0000;
endmodule

module TR (
  input  Clear,
  input  Inc,
  input  Load,
  input  Clock,
  input  [15:0] Bus_IN,
  output [15:0] Bus_OUT
);

  wire or_1_out;
  wire [15:0] adder_1_out, multiplexer_1_out;

  Multiplexer #(.width(16)) multiplexer_1 (
    .in0(Bus_IN), .in1(adder_1_out), .out(multiplexer_1_out), .sel(Inc));  // open: en
  or or_1 (or_1_out, Inc, Load);
  Register #(.width(16)) register_1 (.D(multiplexer_1_out), .en(or_1_out), .Q(Bus_OUT), .clk(Clock), .clr(Clear));
  Adder #(.width(16)) adder_1 (.a(16'h1), .b(Bus_OUT), .out(adder_1_out));  // open: cin, cout
endmodule

module AR (
  input  [15:0] Bus_IN,
  input  Clear,
  input  Clock,
  input  Load,
  input  Inc,
  output [15:0] Bus_OUT
);

  wire or_1_out;
  wire [11:0] adder_1_out, multiplexer_1_out;

  Multiplexer #(.width(12)) multiplexer_1 (
    .in0(Bus_IN[11:0]), .in1(adder_1_out), .out(multiplexer_1_out), .sel(Inc));  // open: en
  or or_1 (or_1_out, Inc, Load);
  Register #(.width(12)) register_1 (.D(multiplexer_1_out), .en(or_1_out), .Q(Bus_OUT[11:0]), .clk(Clock), .clr(Clear));
  Adder #(.width(12)) adder_1 (.a(12'h1), .b(Bus_OUT[11:0]), .out(adder_1_out));  // open: cin, cout

  assign Bus_OUT[15:12] = 4'b0000;
endmodule

module DR (
  input  Inc,
  input  Clear,
  input  Load,
  input  Clock,
  input  [15:0] Bus_IN,
  output [15:0] Bus_OUT
);

  wire or_1_out;
  wire [15:0] adder_1_out, multiplexer_1_out;

  Multiplexer #(.width(16)) multiplexer_1 (
    .in0(Bus_IN), .in1(adder_1_out), .out(multiplexer_1_out), .sel(Inc));  // open: en
  or or_1 (or_1_out, Inc, Load);
  Register #(.width(16), .trigger("falling")) register_1 (
    .D(multiplexer_1_out), .en(or_1_out), .Q(Bus_OUT), .clk(Clock), .clr(Clear));
  Adder #(.width(16)) adder_1 (.a(16'h1), .b(Bus_OUT), .out(adder_1_out));  // open: cin, cout
endmodule

module IR (
  input  Clock,
  input  Load,
  input  [15:0] Bus_IN,
  output I,
  output [15:0] Bus_OUT,
  output S
);

  Register #(.width(16)) register_1 (.D(Bus_IN), .en(Load), .Q(Bus_OUT), .clk(Clock));  // open: clr
  and and_1 (S, Bus_OUT[0], ~Bus_OUT[1], ~Bus_OUT[2], ~Bus_OUT[3], ~Bus_OUT[4], ~Bus_OUT[5], ~Bus_OUT[6], ~Bus_OUT[7], ~Bus_OUT[8], ~Bus_OUT[9], ~Bus_OUT[10], ~Bus_OUT[11], Bus_OUT[12], Bus_OUT[13], Bus_OUT[14], ~Bus_OUT[15]);  // AND_Gate

  assign I = Bus_OUT[15];
endmodule

module E (
  input  E_IN,
  input  Comp,
  input  load,
  input  Clock,
  input  Clear,
  output E_OUT
);

  wire and_1_out, multiplexer_1_out;

  Multiplexer multiplexer_1 (.in0(E_IN), .in1(Comp), .out(multiplexer_1_out), .sel(Comp));  // open: en
  and and_1 (and_1_out, multiplexer_1_out, Comp);
  J_K_Flip_Flop j_k_ff_1 (
    .J(multiplexer_1_out), .clk(Clock), .K(and_1_out), .Q(E_OUT), .en(load), .reset(Clear));  // open: Qn, preset
endmodule

module OUTR (
  input  [15:0] BUS_IN,
  input  L_OUT,
  input  Clock,
  output [3:0] Hex_0,
  output [3:0] Hex_1
);

  wire [15:8] register_1_q;

  Register #(.width(16)) register_1 (
    .D({{8{1'b0}}, BUS_IN[7:0]}), .en(L_OUT), .Q({register_1_q, Hex_1, Hex_0}), .clk(Clock));  // open: clr
endmodule

module R (
  input  [2:0] T_count,
  input  E_IN,
  input  FGO,
  input  FGI,
  output E_OUT
);

  wire and_1_out, and_2_out, and_3_out, decoder_1_out0, decoder_1_out1, decoder_1_out2, or_1_out;

  or or_1 (or_1_out, FGO, FGI);
  and and_1 (and_1_out, ~decoder_1_out0, ~decoder_1_out1, ~decoder_1_out2);  // AND_Gate
  and and_2 (and_2_out, or_1_out, and_1_out, E_IN);
  Decoder #(.select(3)) decoder_1 (
    .out0(decoder_1_out0), .out1(decoder_1_out1), .out2(decoder_1_out2), .sel(T_count));  // open: out3, out4, out5, out6, out7, en
  and and_3 (and_3_out, decoder_1_out2, E_OUT);
  J_K_Flip_Flop j_k_ff_1 (.J(and_2_out), .clk(T_count[0]), .K(and_3_out), .Q(E_OUT));  // open: Qn, preset, en, reset
endmodule

// I EN
module IEN (
  input  EIN_J,
  input  EIN_K,
  input  Clock,
  output EIN_OUT
);

  J_K_Flip_Flop j_k_ff_1 (.J(EIN_J), .clk(Clock), .K(EIN_K), .Q(EIN_OUT));  // open: Qn, preset, en, reset
endmodule

module FGI (
  input  FGI_J,
  input  FGI_K,
  input  Clock,
  output FGI_OUT
);

  J_K_Flip_Flop j_k_ff_1 (.J(FGI_J), .clk(Clock), .K(FGI_K), .Q(FGI_OUT));  // open: Qn, preset, en, reset
endmodule

module FGO (
  input  FGO_J,
  input  FGO_K,
  input  Clock,
  output FGO_OUT
);

  J_K_Flip_Flop j_k_ff_1 (.J(FGO_J), .clk(Clock), .K(FGO_K), .Q(FGO_OUT));  // open: Qn, preset, en, reset
endmodule

module T_count (
  input  Clear,
  input  Clock,
  output [2:0] OUT
);

  wire and_1_out, or_1_out;
  wire [2:0] adder_1_out;

  Register #(.width(3)) register_1 (.D(adder_1_out), .Q(OUT), .clk(Clock), .clr(or_1_out));  // open: en
  or or_1 (or_1_out, Clear, and_1_out);
  and and_1 (and_1_out, OUT[0], OUT[1], OUT[2]);
  Adder #(.width(3)) adder_1 (.a(3'b001), .b(OUT), .out(adder_1_out));  // open: cin, cout
endmodule

// BUS Control
module Bus_Select_control (
  input  [15:0] IR,
  input  [3:0] T,
  input  R,
  output [2:0] Bus_Select
);

  wire and_2_out, and_3_out, and_4_out, and_5_out, and_6_out, and_7_out, and_8_out, and_9_out, and_10_out,
       and_11_out, and_12_out, and_13_out, and_14_out, decoder_1_out0, decoder_1_out1, decoder_1_out2,
       decoder_1_out3, decoder_1_out4, decoder_1_out5, decoder_1_out6, decoder_1_out7, decoder_2_out0,
       decoder_2_out1, decoder_2_out2, decoder_2_out3, decoder_2_out4, decoder_2_out5, decoder_2_out6,
       decoder_2_out7, or_1_out, or_2_out, or_3_out, or_4_out, or_5_out, or_6_out, p;
  wire [2:0] priority_encoder_1_out;

  Decoder #(.select(3)) decoder_1 (
    .out0(decoder_1_out0), .out1(decoder_1_out1), .out2(decoder_1_out2), .out3(decoder_1_out3),
    .out4(decoder_1_out4), .out5(decoder_1_out5), .out6(decoder_1_out6), .out7(decoder_1_out7), .sel(T[2:0]));  // open: en
  Decoder #(.select(3)) decoder_2 (
    .out0(decoder_2_out0), .out1(decoder_2_out1), .out2(decoder_2_out2), .out3(decoder_2_out3),
    .out4(decoder_2_out4), .out5(decoder_2_out5), .out6(decoder_2_out6), .out7(decoder_2_out7),
    .sel(IR[14:12]));  // open: en
  and and_1 (p, decoder_2_out7, IR[15], decoder_1_out3);
  and and_2 (and_2_out, decoder_2_out5, decoder_1_out4);
  and and_3 (and_3_out, decoder_1_out4, decoder_2_out4);
  and and_4 (and_4_out, decoder_2_out5, decoder_1_out5);
  and and_5 (and_5_out, decoder_2_out6, decoder_1_out6);
  and and_6 (and_6_out, decoder_2_out2, decoder_1_out5);
  and and_7 (and_7_out, decoder_2_out3, decoder_1_out4);
  and and_8 (and_8_out, IR[10], p);
  and and_9 (and_9_out, decoder_1_out2, ~R);  // AND_Gate
  and and_10 (and_10_out, decoder_1_out1, R);
  and and_11 (and_11_out, decoder_1_out1, ~R);  // AND_Gate
  and and_12 (and_12_out, ~decoder_2_out7, IR[15], decoder_1_out3);  // AND_Gate
  or or_1 (or_1_out, decoder_2_out0, decoder_2_out1, decoder_2_out2, decoder_2_out6);
  and and_13 (and_13_out, or_1_out, decoder_1_out4);
  or or_2 (or_2_out, decoder_1_out0, and_2_out);
  or or_3 (or_3_out, and_3_out, and_4_out);
  or or_4 (or_4_out, and_5_out, and_6_out);
  or or_5 (or_5_out, and_7_out, and_8_out);
  or or_6 (or_6_out, and_11_out, and_12_out, and_13_out);
  and and_14 (and_14_out, ~or_3_out, ~or_2_out, ~or_4_out, ~or_5_out, ~and_9_out, ~and_10_out, ~or_6_out);  // AND_Gate
  Priority_Encoder priority_encoder_1 (
    .in0(and_14_out), .in1(or_3_out), .in2(or_2_out), .in3(or_4_out), .in4(or_5_out), .in5(and_9_out),
    .in6(and_10_out), .in7(or_6_out), .out(priority_encoder_1_out));  // open: en_in, gs, en_out
  Multiplexer #(.select(3), .width(3)) multiplexer_1 (
    .in0(3'b000), .in1(3'b001), .in2(3'b010), .in3(3'b011), .in4(3'b100), .in5(3'b101), .in6(3'b110),
    .in7(3'b111), .out(Bus_Select), .sel(priority_encoder_1_out));  // open: en
endmodule

// SC/T control
module Clear_T_count_control (
  input  [15:0] IR,
  input  [3:0] T,
  input  R,
  output T_count_clear
);

  wire and_1_out, and_2_out, and_3_out, and_4_out, and_5_out, and_6_out, and_7_out, decoder_1_out0,
       decoder_1_out1, decoder_1_out2, decoder_1_out3, decoder_1_out4, decoder_1_out5, decoder_1_out6,
       decoder_1_out7, decoder_2_out0, decoder_2_out1, decoder_2_out2, decoder_2_out3, decoder_2_out4,
       decoder_2_out5, decoder_2_out6, decoder_2_out7, or_1_out;

  Decoder #(.select(3)) decoder_1 (
    .out0(decoder_1_out0), .out1(decoder_1_out1), .out2(decoder_1_out2), .out3(decoder_1_out3),
    .out4(decoder_1_out4), .out5(decoder_1_out5), .out6(decoder_1_out6), .out7(decoder_1_out7), .sel(T[2:0]));  // open: en
  Decoder #(.select(3)) decoder_2 (
    .out0(decoder_2_out0), .out1(decoder_2_out1), .out2(decoder_2_out2), .out3(decoder_2_out3),
    .out4(decoder_2_out4), .out5(decoder_2_out5), .out6(decoder_2_out6), .out7(decoder_2_out7),
    .sel(IR[14:12]));  // open: en
  and and_1 (and_1_out, decoder_2_out7, ~IR[15], decoder_1_out4);  // AND_Gate
  and and_2 (and_2_out, decoder_1_out4, IR[15], decoder_2_out7);
  and and_3 (and_3_out, decoder_1_out3, R);
  or or_1 (or_1_out, decoder_2_out0, decoder_2_out1, decoder_2_out2, decoder_2_out5);
  and and_4 (and_4_out, or_1_out, decoder_1_out6);
  and and_5 (and_5_out, decoder_1_out5, decoder_2_out3);
  and and_6 (and_6_out, decoder_2_out4, decoder_1_out5);
  and and_7 (and_7_out, decoder_2_out6, decoder_1_out7);
  or or_2 (T_count_clear, and_1_out, and_3_out, and_4_out, and_5_out, and_6_out, and_7_out, and_2_out);
endmodule

module AR_control (
  input  [15:0] IR,
  input  [3:0] T,
  input  R,
  output LD,
  output Clr,
  output Inc
);

  wire and_1_out, and_2_out, and_3_out, decoder_1_out0, decoder_1_out1, decoder_1_out2, decoder_1_out3,
       decoder_1_out4, decoder_1_out5, decoder_1_out6, decoder_1_out7, decoder_2_out0, decoder_2_out1,
       decoder_2_out2, decoder_2_out3, decoder_2_out4, decoder_2_out5, decoder_2_out6, decoder_2_out7;

  Decoder #(.select(3)) decoder_1 (
    .out0(decoder_1_out0), .out1(decoder_1_out1), .out2(decoder_1_out2), .out3(decoder_1_out3),
    .out4(decoder_1_out4), .out5(decoder_1_out5), .out6(decoder_1_out6), .out7(decoder_1_out7), .sel(T[2:0]));  // open: en
  Decoder #(.select(3)) decoder_2 (
    .out0(decoder_2_out0), .out1(decoder_2_out1), .out2(decoder_2_out2), .out3(decoder_2_out3),
    .out4(decoder_2_out4), .out5(decoder_2_out5), .out6(decoder_2_out6), .out7(decoder_2_out7),
    .sel(IR[14:12]));  // open: en
  and and_1 (and_1_out, ~R, decoder_1_out0);  // AND_Gate
  and and_2 (and_2_out, ~decoder_2_out7, IR[15], decoder_1_out3);  // AND_Gate
  and and_3 (and_3_out, ~R, decoder_1_out2);  // AND_Gate
  and and_4 (Clr, R, decoder_1_out0);
  and and_5 (Inc, decoder_2_out5, decoder_1_out4);
  or or_1 (LD, and_1_out, and_2_out, and_3_out);
endmodule

module IR_control (
  input  [3:0] T,
  input  R,
  output LD
);

  wire decoder_1_out0, decoder_1_out1, decoder_1_out2, decoder_1_out3, decoder_1_out4, decoder_1_out5,
       decoder_1_out6, decoder_1_out7;

  Decoder #(.select(3)) decoder_1 (
    .out0(decoder_1_out0), .out1(decoder_1_out1), .out2(decoder_1_out2), .out3(decoder_1_out3),
    .out4(decoder_1_out4), .out5(decoder_1_out5), .out6(decoder_1_out6), .out7(decoder_1_out7), .sel(T[2:0]));  // open: en
  and and_1 (LD, ~R, decoder_1_out1);  // AND_Gate
endmodule

module TR_control (
  input  [3:0] T,
  input  R,
  output LD
);

  wire decoder_1_out0, decoder_1_out1, decoder_1_out2, decoder_1_out3, decoder_1_out4, decoder_1_out5,
       decoder_1_out6, decoder_1_out7;

  Decoder #(.select(3)) decoder_1 (
    .out0(decoder_1_out0), .out1(decoder_1_out1), .out2(decoder_1_out2), .out3(decoder_1_out3),
    .out4(decoder_1_out4), .out5(decoder_1_out5), .out6(decoder_1_out6), .out7(decoder_1_out7), .sel(T[2:0]));  // open: en
  and and_1 (LD, R, decoder_1_out0);
endmodule

module DR_control (
  input  [15:0] IR,
  input  [3:0] T,
  output LD,
  output Inc
);

  wire decoder_1_out0, decoder_1_out1, decoder_1_out2, decoder_1_out3, decoder_1_out4, decoder_1_out5,
       decoder_1_out6, decoder_1_out7, decoder_2_out0, decoder_2_out1, decoder_2_out2, decoder_2_out3,
       decoder_2_out4, decoder_2_out5, decoder_2_out6, decoder_2_out7, or_1_out;

  Decoder #(.select(3)) decoder_1 (
    .out0(decoder_1_out0), .out1(decoder_1_out1), .out2(decoder_1_out2), .out3(decoder_1_out3),
    .out4(decoder_1_out4), .out5(decoder_1_out5), .out6(decoder_1_out6), .out7(decoder_1_out7), .sel(T[2:0]));  // open: en
  Decoder #(.select(3)) decoder_2 (
    .out0(decoder_2_out0), .out1(decoder_2_out1), .out2(decoder_2_out2), .out3(decoder_2_out3),
    .out4(decoder_2_out4), .out5(decoder_2_out5), .out6(decoder_2_out6), .out7(decoder_2_out7),
    .sel(IR[14:12]));  // open: en
  and and_1 (Inc, decoder_2_out6, decoder_1_out5);
  or or_1 (or_1_out, decoder_2_out0, decoder_2_out1, decoder_2_out2, decoder_2_out6);
  and and_2 (LD, decoder_1_out4, or_1_out);
endmodule

module PC_control (
  input  R,
  input  [15:0] IR,
  input  [15:0] DR,
  input  [15:0] AC,
  input  [3:0] T,
  input  FGI,
  input  FGO,
  input  E,
  output LD,
  output Inc,
  output Clr
);

  wire and_3_out, and_4_out, and_5_out, and_6_out, and_7_out, and_8_out, and_9_out, and_10_out, and_11_out,
       and_12_out, and_13_out, decoder_1_out0, decoder_1_out1, decoder_1_out2, decoder_1_out3,
       decoder_1_out4, decoder_1_out5, decoder_1_out6, decoder_1_out7, decoder_2_out0, decoder_2_out1,
       decoder_2_out2, decoder_2_out3, decoder_2_out4, decoder_2_out5, decoder_2_out6, decoder_2_out7,
       not_1_out, not_2_out, or_2_out, or_4_out, p, r_t;

  Decoder #(.select(3)) decoder_1 (
    .out0(decoder_1_out0), .out1(decoder_1_out1), .out2(decoder_1_out2), .out3(decoder_1_out3),
    .out4(decoder_1_out4), .out5(decoder_1_out5), .out6(decoder_1_out6), .out7(decoder_1_out7), .sel(T[2:0]));  // open: en
  Decoder #(.select(3)) decoder_2 (
    .out0(decoder_2_out0), .out1(decoder_2_out1), .out2(decoder_2_out2), .out3(decoder_2_out3),
    .out4(decoder_2_out4), .out5(decoder_2_out5), .out6(decoder_2_out6), .out7(decoder_2_out7),
    .sel(IR[14:12]));  // open: en
  and and_1 (p, decoder_2_out7, IR[15], decoder_1_out3);
  and and_2 (r_t, decoder_2_out7, ~IR[15], decoder_1_out3);  // AND_Gate
  not not_1 (not_1_out, or_2_out);
  and and_3 (and_3_out, decoder_2_out4, decoder_1_out4);
  or or_1 (LD, and_3_out, and_4_out);
  and and_4 (and_4_out, decoder_2_out5, decoder_1_out5);
  and and_5 (and_5_out, ~R, decoder_1_out1);  // AND_Gate
  and and_6 (and_6_out, R, decoder_1_out2);
  and and_7 (and_7_out, decoder_1_out6, decoder_2_out6, not_1_out);
  and and_8 (and_8_out, ~AC[15], IR[4], r_t);  // AND_Gate
  and and_9 (and_9_out, AC[15], IR[3], r_t);
  and and_10 (and_10_out, not_2_out, IR[2], r_t);
  and and_11 (and_11_out, ~E, IR[1], r_t);  // AND_Gate
  and and_12 (and_12_out, IR[9], FGI, p);
  and and_13 (and_13_out, IR[8], FGO, p);
  and and_14 (Clr, R, decoder_1_out1);
  or or_2 (or_2_out, DR[15], DR[14], DR[13], DR[12], DR[11], DR[10], DR[9], DR[8], DR[7], DR[6], DR[5], DR[4], DR[3], DR[2], DR[1], DR[0]);
  not not_2 (not_2_out, or_4_out);
  or or_3 (Inc, and_5_out, and_6_out, and_7_out, and_8_out, and_9_out, and_10_out, and_11_out, and_12_out, and_13_out);
  or or_4 (or_4_out, AC[15], AC[14], AC[13], AC[12], AC[11], AC[10], AC[9], AC[8], AC[7], AC[6], AC[5], AC[4], AC[3], AC[2], AC[1], AC[0]);
endmodule

module AC_control (
  input  [15:0] IR,
  input  [3:0] T,
  output Clr,
  output Inc
);

  wire decoder_1_out0, decoder_1_out1, decoder_1_out2, decoder_1_out3, decoder_1_out4, decoder_1_out5,
       decoder_1_out6, decoder_1_out7, decoder_2_out0, decoder_2_out1, decoder_2_out2, decoder_2_out3,
       decoder_2_out4, decoder_2_out5, decoder_2_out6, decoder_2_out7, p, r;

  Decoder #(.select(3)) decoder_1 (
    .out0(decoder_1_out0), .out1(decoder_1_out1), .out2(decoder_1_out2), .out3(decoder_1_out3),
    .out4(decoder_1_out4), .out5(decoder_1_out5), .out6(decoder_1_out6), .out7(decoder_1_out7), .sel(T[2:0]));  // open: en
  Decoder #(.select(3)) decoder_2 (
    .out0(decoder_2_out0), .out1(decoder_2_out1), .out2(decoder_2_out2), .out3(decoder_2_out3),
    .out4(decoder_2_out4), .out5(decoder_2_out5), .out6(decoder_2_out6), .out7(decoder_2_out7),
    .sel(IR[14:12]));  // open: en
  and and_1 (p, decoder_1_out3, IR[15], decoder_2_out7);
  and and_2 (r, decoder_1_out3, ~IR[15], decoder_2_out7);  // AND_Gate
  and and_3 (Clr, IR[11], r);
  and and_4 (Inc, IR[5], r);
endmodule

module FGI_O___IEN_control (
  input  [15:0] IR,
  input  [3:0] T,
  input  [7:0] INPR,
  input  R,
  output IEN_J,
  output IEN_K,
  output FGI_J,
  output FGI_K,
  output FGO_J,
  output FGO_K
);

  wire and_3_out, and_4_out, decoder_1_out1, decoder_1_out2, decoder_1_out3, decoder_1_out4, decoder_1_out5,
       decoder_1_out6, decoder_1_out7, decoder_2_out0, decoder_2_out1, decoder_2_out2, decoder_2_out3,
       decoder_2_out4, decoder_2_out5, decoder_2_out6, decoder_2_out7, p;

  Decoder #(.select(3)) decoder_1 (
    .out0(FGO_J), .out1(decoder_1_out1), .out2(decoder_1_out2), .out3(decoder_1_out3), .out4(decoder_1_out4),
    .out5(decoder_1_out5), .out6(decoder_1_out6), .out7(decoder_1_out7), .sel(T[2:0]));  // open: en
  Decoder #(.select(3)) decoder_2 (
    .out0(decoder_2_out0), .out1(decoder_2_out1), .out2(decoder_2_out2), .out3(decoder_2_out3),
    .out4(decoder_2_out4), .out5(decoder_2_out5), .out6(decoder_2_out6), .out7(decoder_2_out7),
    .sel(IR[14:12]));  // open: en
  and and_1 (p, IR[15], decoder_2_out7, decoder_1_out3);
  and and_2 (IEN_J, IR[7], p);
  and and_3 (and_3_out, R, decoder_1_out2);
  and and_4 (and_4_out, IR[6], p);
  or or_1 (FGI_J, INPR[0], INPR[1], INPR[2], INPR[3], INPR[4], INPR[5], INPR[6], INPR[7]);
  and and_5 (FGI_K, IR[11], p);
  and and_6 (FGO_K, IR[10], p);
  or or_2 (IEN_K, and_3_out, and_4_out);
endmodule

// OUTR control
module OUTPR_control (
  input  [15:0] IR,
  input  [3:0] T,
  output LD
);

  wire decoder_1_out0, decoder_1_out1, decoder_1_out2, decoder_1_out3, decoder_1_out4, decoder_1_out5,
       decoder_1_out6, decoder_1_out7, decoder_2_out0, decoder_2_out1, decoder_2_out2, decoder_2_out3,
       decoder_2_out4, decoder_2_out5, decoder_2_out6, decoder_2_out7, p;

  Decoder #(.select(3)) decoder_1 (
    .out0(decoder_1_out0), .out1(decoder_1_out1), .out2(decoder_1_out2), .out3(decoder_1_out3),
    .out4(decoder_1_out4), .out5(decoder_1_out5), .out6(decoder_1_out6), .out7(decoder_1_out7), .sel(T[2:0]));  // open: en
  Decoder #(.select(3)) decoder_2 (
    .out0(decoder_2_out0), .out1(decoder_2_out1), .out2(decoder_2_out2), .out3(decoder_2_out3),
    .out4(decoder_2_out4), .out5(decoder_2_out5), .out6(decoder_2_out6), .out7(decoder_2_out7),
    .sel(IR[14:12]));  // open: en
  and and_1 (p, decoder_1_out3, IR[15], decoder_2_out7);
  and and_2 (LD, IR[10], p);
endmodule

module E_control (
  input  [15:0] IR,
  input  [3:0] T,
  output Comp,
  output Clear,
  output Load
);

  wire and_5_out, and_6_out, and_7_out, decoder_1_out0, decoder_1_out1, decoder_1_out2, decoder_1_out3,
       decoder_1_out4, decoder_1_out5, decoder_1_out6, decoder_1_out7, decoder_2_out0, decoder_2_out1,
       decoder_2_out2, decoder_2_out3, decoder_2_out4, decoder_2_out5, decoder_2_out6, decoder_2_out7, p, r;

  Decoder #(.select(3)) decoder_1 (
    .out0(decoder_1_out0), .out1(decoder_1_out1), .out2(decoder_1_out2), .out3(decoder_1_out3),
    .out4(decoder_1_out4), .out5(decoder_1_out5), .out6(decoder_1_out6), .out7(decoder_1_out7), .sel(T[2:0]));  // open: en
  Decoder #(.select(3)) decoder_2 (
    .out0(decoder_2_out0), .out1(decoder_2_out1), .out2(decoder_2_out2), .out3(decoder_2_out3),
    .out4(decoder_2_out4), .out5(decoder_2_out5), .out6(decoder_2_out6), .out7(decoder_2_out7),
    .sel(IR[14:12]));  // open: en
  and and_1 (p, decoder_1_out3, IR[15], decoder_2_out7);
  and and_2 (r, decoder_1_out3, ~IR[15], decoder_2_out7);  // AND_Gate
  and and_3 (Comp, IR[8], r);
  and and_4 (Clear, IR[10], r);
  and and_5 (and_5_out, decoder_2_out1, decoder_1_out5);
  and and_6 (and_6_out, IR[7], r);
  and and_7 (and_7_out, IR[6], r);
  or or_1 (Load, and_5_out, and_6_out, and_7_out);
endmodule

module Memory_control (
  input  [15:0] IR,
  input  [3:0] T,
  input  R,
  output Load
);

  wire and_1_out, and_2_out, and_3_out, and_4_out, decoder_1_out0, decoder_1_out1, decoder_1_out2,
       decoder_1_out3, decoder_1_out4, decoder_1_out5, decoder_1_out6, decoder_1_out7, decoder_2_out0,
       decoder_2_out1, decoder_2_out2, decoder_2_out3, decoder_2_out4, decoder_2_out5, decoder_2_out6,
       decoder_2_out7, or_1_out;

  Decoder #(.select(3)) decoder_1 (
    .out0(decoder_1_out0), .out1(decoder_1_out1), .out2(decoder_1_out2), .out3(decoder_1_out3),
    .out4(decoder_1_out4), .out5(decoder_1_out5), .out6(decoder_1_out6), .out7(decoder_1_out7), .sel(T[2:0]));  // open: en
  Decoder #(.select(3)) decoder_2 (
    .out0(decoder_2_out0), .out1(decoder_2_out1), .out2(decoder_2_out2), .out3(decoder_2_out3),
    .out4(decoder_2_out4), .out5(decoder_2_out5), .out6(decoder_2_out6), .out7(decoder_2_out7),
    .sel(IR[14:12]));  // open: en
  and and_1 (and_1_out, R, decoder_1_out1);
  and and_2 (and_2_out, decoder_2_out3, decoder_1_out4);
  and and_3 (and_3_out, decoder_2_out5, decoder_1_out4);
  and and_4 (and_4_out, decoder_2_out6, decoder_1_out6);
  or or_1 (or_1_out, and_1_out, and_2_out, and_3_out, and_4_out);
  not not_1 (Load, or_1_out);
endmodule
